// Logisim project hkcpu.circ as structural Verilog: 9 circuits, main circuit main
module main (
  input  RST,
  output [7:0] out_2
);

  wire and_1_out, and_2_out, counter_1_carry, d_ff_1_q, or_1_out, or_2_out, por_1_out, s_r_ff_1_q,
       s_r_ff_1_qn;
  wire [7:0] counter_1_q, cpu_1_mda, cpu_1_mdo, ram_1_dout, rom_1_data;
  wire [9:8] cpu_1_mie;
  wire [9:9] CLK_out;
  wire [17:0] multiplexer_1_out;

  POR #(.PorHighDuration(1)) por_1 (.out(por_1_out));
  Clock CLK (.out(CLK_out[9]));
  S_R_Flip_Flop s_r_ff_1 (.Q(s_r_ff_1_q), .Qn(s_r_ff_1_qn), .preset(and_1_out), .reset(d_ff_1_q));  // open: S, clk, R
  and and_1 (and_1_out, por_1_out, s_r_ff_1_qn);
  D_Flip_Flop d_ff_1 (.clk(CLK_out[9]), .D(counter_1_carry), .Q(d_ff_1_q));  // open: Qn, preset, reset
  Counter counter_1 (
    .Q(counter_1_q), .carry(counter_1_carry), .clk(CLK_out[9]), .clr(or_1_out));  // open: load, D, count, up
  or or_1 (or_1_out, s_r_ff_1_qn, and_1_out);
  or or_2 (or_2_out, RST, s_r_ff_1_q);
  and and_2 (and_2_out, CLK_out[9], ~s_r_ff_1_q);  // AND_Gate
  Multiplexer #(.width(18)) multiplexer_1 (
    .in0({cpu_1_mdo, cpu_1_mie, cpu_1_mda}), .in1({rom_1_data, CLK_out[9], 1'b1, counter_1_q}),
    .out(multiplexer_1_out), .sel(s_r_ff_1_q));
  RAM #(.asyncread("true")) ram_1 (
    .addr(multiplexer_1_out[7:0]), .we(multiplexer_1_out[8]), .clk(multiplexer_1_out[9]),
    .din(multiplexer_1_out[17:10]), .dout(ram_1_dout));  // open: oe
  ROM rom_1 (.addr(counter_1_q), .data(rom_1_data));
  cpu cpu_1 (
    .CLK(and_2_out), .RST(or_2_out), .MDI(ram_1_dout), .MCLK(cpu_1_mie[9]), .MDA(cpu_1_mda),
    .MIE(cpu_1_mie[8]), .MDO(cpu_1_mdo), .DO(out_2));
endmodule

module cpu (
  input  CLK,
  input  RST,
  input  [7:0] MDI,
  output MCLK,
  output [7:0] MDA,
  output MIE,
  output [7:0] MDO,
  output [7:0] DO
);

  wire or_1_out;
  wire [2:0] alu_1_flgo, logiccontrol_1_lco_2, logiccontrol_1_lco_3, logiccontrol_1_lco_6;
  wire [3:0] logiccontrol_1_lco_4;
  wire [5:0] logiccontrol_1_lco_5;
  wire [7:0] pull_resistor_1_node, regs_1_abps, regs_1_bbps;
  wire [21:0] logiccontrol_1_lco;

  or or_1 (or_1_out, RST, logiccontrol_1_lco[21]);
  LogicClock logicclock_1 (.CLKI(CLK), .HLT(logiccontrol_1_lco[20]), .CLKO(MCLK));
  Pull_Resistor pull_resistor_1 (.node(pull_resistor_1_node));
  LogicCounter logiccounter_1 (
    .CLK(MCLK), .RST(or_1_out), .BUSI(pull_resistor_1_node), .CE(logiccontrol_1_lco_6[2]),
    .CO(logiccontrol_1_lco_6[1]), .CL(logiccontrol_1_lco_6[0]), .BUSO(pull_resistor_1_node));
  regs regs_1 (
    .CLK(MCLK), .RST(or_1_out), .BUSI(pull_resistor_1_node), .RI(logiccontrol_1_lco_5[5:3]),
    .RO(logiccontrol_1_lco_5[2:0]), .ABPS(regs_1_abps), .BBPS(regs_1_bbps), .BUSO(pull_resistor_1_node));
  alu alu_1 (
    .CLK(MCLK), .RST(or_1_out), .A(regs_1_abps), .B(regs_1_bbps), .AOP(logiccontrol_1_lco_4[3:1]),
    .AO(logiccontrol_1_lco_4[0]), .FLGO(alu_1_flgo), .BUSO(pull_resistor_1_node));
  LogicControl logiccontrol_1 (
    .CLK(MCLK), .RST(or_1_out), .BUSI(pull_resistor_1_node), .FLGI(alu_1_flgo),
    .IRI(logiccontrol_1_lco_3[2]), .ARI(logiccontrol_1_lco_3[1]), .ARO(logiccontrol_1_lco_3[0]),
    .LCO({logiccontrol_1_lco[21:20], logiccontrol_1_lco_6, logiccontrol_1_lco_5, logiccontrol_1_lco_4, logiccontrol_1_lco_3, logiccontrol_1_lco_2, logiccontrol_1_lco[0]}),
    .BUSO(pull_resistor_1_node));
  memory memory_1 (
    .CLK(MCLK), .RST(or_1_out), .BUSI(pull_resistor_1_node), .CMDI(MDI), .MAI(logiccontrol_1_lco_2[2]),
    .MI(logiccontrol_1_lco_2[1]), .MO(logiccontrol_1_lco_2[0]), .CMA(MDA), .CMI(MIE), .CMDO(MDO),
    .BUSO(pull_resistor_1_node));
  LogicOutput logicoutput_1 (
    .CLK(MCLK), .RST(or_1_out), .BUSI(pull_resistor_1_node), .OE(logiccontrol_1_lco[0]), .LogicOut(DO));
endmodule

module alu (
  input  CLK,
  input  RST,
  input  [7:0] A,
  input  [7:0] B,
  input  [2:0] AOP,
  input  AO,
  output [2:0] FLGO,
  output [7:0] BUSO
);

  wire not_1_out;
  wire [2:0] comparator_1_gt;
  wire [7:0] adder_1_out, divider_1_out, multiplexer_1_out, multiplier_1_out, subtractor_1_out;

  Comparator comparator_1 (.a(A), .b(B), .gt(comparator_1_gt[0]), .eq(comparator_1_gt[1]), .lt(comparator_1_gt[2]));
  Adder adder_1 (.a(A), .b(B), .out(adder_1_out));  // open: cin, cout
  Subtractor subtractor_1 (.a(A), .b(B), .out(subtractor_1_out));  // open: bin, bout
  Multiplier multiplier_1 (.a(A), .b(B), .out(multiplier_1_out));  // open: cin, cout
  Divider divider_1 (.a(A), .b(B), .out(divider_1_out));  // open: upper, rem
  Register #(.width(3)) register_1 (.D(comparator_1_gt), .Q(FLGO), .clk(CLK), .clr(RST));  // open: en
  assign BUSO = AO ? multiplexer_1_out : 8'bz;  // Controlled_Buffer controlled_buffer_1
  Multiplexer #(.enable("true"), .select(2), .width(8)) multiplexer_1 (
    .in0(adder_1_out), .in1(subtractor_1_out), .in2(multiplier_1_out), .in3(divider_1_out),
    .out(multiplexer_1_out), .sel(AOP[1:0]), .en(not_1_out));
  not not_1 (not_1_out, AOP[2]);
endmodule

module LogicClock (
  input  CLKI,
  input  HLT,
  output CLKO
);

  and and_1 (CLKO, CLKI, ~HLT);  // AND_Gate
endmodule

module LogicCounter (
  input  CLK,
  input  RST,
  input  [7:0] BUSI,
  input  CE,
  input  CO,
  input  CL,
  output [7:0] BUSO
);

  wire [7:0] counter_1_q;

  Counter counter_1 (.load(CL), .D(BUSI), .count(CE), .Q(counter_1_q), .clk(CLK), .clr(RST));  // open: carry, up
  assign BUSO = CO ? counter_1_q : 8'bz;  // Controlled_Buffer controlled_buffer_1
endmodule

module regs (
  input  CLK,
  input  RST,
  input  [7:0] BUSI,
  input  [2:0] RI,
  input  [2:0] RO,
  output [7:0] ABPS,
  output [7:0] BBPS,
  output [7:0] BUSO
);

  wire [7:0] register_3_q;

  Register register_1 (.D(BUSI), .en(RI[2]), .Q(ABPS), .clk(CLK), .clr(RST));
  Register register_2 (.D(BUSI), .en(RI[1]), .Q(BBPS), .clk(CLK), .clr(RST));
  Register register_3 (.D(BUSI), .en(RI[0]), .Q(register_3_q), .clk(CLK), .clr(RST));
  assign BUSO = RO[2] ? ABPS : 8'bz;  // Controlled_Buffer controlled_buffer_1
  assign BUSO = RO[1] ? BBPS : 8'bz;  // Controlled_Buffer controlled_buffer_2
  assign BUSO = RO[0] ? register_3_q : 8'bz;  // Controlled_Buffer controlled_buffer_3
endmodule

module memory (
  input  CLK,
  input  RST,
  input  [7:0] BUSI,
  input  [7:0] CMDI,
  input  MAI,
  input  MI,
  input  MO,
  output [7:0] CMA,
  output CMI,
  output [7:0] CMDO,
  output [7:0] BUSO
);

  Register register_1 (.D(BUSI), .en(MAI), .Q(CMA), .clk(CLK), .clr(RST));
  assign BUSO = MO ? CMDI : 8'bz;  // Controlled_Buffer controlled_buffer_1

  assign CMDO = BUSI;
  assign CMI = MI;
endmodule

module LogicOutput (
  input  CLK,
  input  RST,
  input  [7:0] BUSI,
  input  OE,
  output [7:0] LogicOut
);

  Register register_1 (.D(BUSI), .en(OE), .Q(LogicOut), .clk(CLK), .clr(RST));
endmodule

module LogicControl (
  input  CLK,
  input  RST,
  input  [7:0] BUSI,
  input  [2:0] FLGI,
  input  IRI,
  input  ARI,
  input  ARO,
  output [21:0] LCO,
  output [7:0] BUSO
);

  wire [2:0] counter_1_q;
  wire [7:0] register_1_q, register_2_q;

  Counter #(.max('h7), .trigger("falling"), .width(3)) counter_1 (
    .Q(counter_1_q), .clk(CLK), .clr(RST));  // open: load, D, count, carry, up
  Register register_1 (.D(BUSI), .en(IRI), .Q(register_1_q), .clk(CLK), .clr(RST));
  assign BUSO = ARO ? register_2_q : 8'bz;  // Controlled_Buffer controlled_buffer_1
  Register register_2 (.D(BUSI), .en(ARI), .Q(register_2_q), .clk(CLK), .clr(RST));
  PLA #(.in_width(14), .out_width(22), .\table ("xxxxxxxxxxx000 0001000000000000001000\nxxxxxxxxxxx001 0010000000000001000010\n00000000xxx010 0000000000000000000000\n00000001xxx010 0000000100000010000000\n00000010xxx010 0000000100000110000000\n00000011xxx010 0000000100001010000000\n00000100xxx010 0000000100001110000000\n00000101xxx010 0001000000000000001000\n00000101xxx011 0010000000000000100010\n00000101xxx100 0000000000000000011000\n00000101xxx101 0000010000000000000010\n00000110xxx010 0001000000000000001000\n00000110xxx011 0010000000000000100010\n00000110xxx100 0000000000000000011000\n00000110xxx101 0000001000000000000010\n00000111xxx010 0001000000000000001000\n00000111xxx011 0010000000000000100010\n00000111xxx100 0000000000000000011000\n00000111xxx101 0000000100000000000010\n00001000xxx010 0001000000000000001000\n00001000xxx011 0010000000000000100010\n00001000xxx100 0000000000000000011000\n00001000xxx101 0000000010000000000100\n00001001xxx010 0001000000000000001000\n00001001xxx011 0010000000000000100010\n00001001xxx100 0000000000000000011000\n00001001xxx101 0000000001000000000100\n00001010xxx010 0001000000000000001000\n00001010xxx011 0010000000000000100010\n00001010xxx100 0000000000000000011000\n00001010xxx101 0000000000100000000100\n00001011xxx010 0000001010000000000000\n00001100xxx010 0000000110000000000000\n00001101xxx010 0000010001000000000000\n00001110xxx010 0000000101000000000000\n00001111xxx010 0000010000100000000000\n00010000xxx010 0000001000100000000000\n00010001xxx010 0001000000000000001000\n00010001xxx011 0000100000000000000010\n00010010xxx010 0000000000010000000000\n00010011010010 0001000000000000001000\n00010011010011 0000100000000000000010\n00010100x0x010 0001000000000000001000\n00010100x0x011 0000100000000000000010\n00010101100010 0001000000000000001000\n00010101100011 0000100000000000000010\n00010110001010 0001000000000000001000\n00010110001011 0000100000000000000010\n00010111xxx010 0001000000000000001000\n00010111xxx011 0010000000000000100010\n00010111xxx100 0000000000000000011000\n00010111xxx101 0000000000000000000011\n11111110xxx010 1000000000000000000000\n11111111xxx010 0100000000000000000000")) pla_1 (
    .in({register_1_q, FLGI, counter_1_q}), .out(LCO));
endmodule
